# Fritzing sketch RTC_DHT22_fritzing (saved by Fritzing 0.9.8b)
breadboards: 1

parts:
  Компонент1 = Adafruit Proto Shield R3 [part_number="Adafruit #2077"]
  RHT1 = Humidity and Temperature Sensor RHT03
  ZS-042_RTC1 = ZS-042 RTC Module
  microSD1 = MicroSD Card Module

nets:
  N1: Компонент1.D4, microSD1.CS
  VCC: Компонент1.+5V, RHT1.Vcc, ZS-042_RTC1.VCC, microSD1.VCC
  N2: Компонент1.A4, ZS-042_RTC1.SDA
  N3: Компонент1.A5, ZS-042_RTC1.SCL
  N4: Компонент1.D2, RHT1.Data-signal
  N5: Компонент1.D11, microSD1.MOSI
  N6: Компонент1.D12, microSD1.MISO
  N7: Компонент1.D13, microSD1.SCK
  GND: Компонент1.GND, RHT1.GND_2, ZS-042_RTC1.GND, microSD1.GND

custom parts:
  Adafruit Proto Shield R3: This prototyping shield is the best out there (well, we think so, at least), and now is even better with Version R3 - updated for the most compatibility with just about all the Arduinos! It works with UNO, Mega, Leonardo, NG, Diecimila, Duemilanove, and compatible Arduinos. Yun's and Arduino Ethernets have a chunky Ethernet jack that gets in the way of stacking, you can use the stacking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

// code stored in the sketch: test.ino
//include relevant libraries for the Arduino, sensor and Real time clock (RTC)
#include <DHT.h>
#include <DHT_U.h>
#include <SPI.h>
#include <SD.h>
#include <Wire.h>
#include "RTClib.h" 


//define DHT pin
#define DHTPIN 2        //  pin the sensor is connected to on arduino (can be any number from 2 - 13)
#define DHTTYPE DHT22   // DHT22 is the type of temperature sensor we are using  

File myFile;

// initialize DHT sensor for normal 16mhz Arduino
DHT dht(DHTPIN, DHTTYPE);
RTC_DS3231 RTC;


void setup () {   // setup function runs once

  
  
  //initializing the DHT and RTC
  dht.begin();
  Wire.begin();
  RTC.begin();

  // Check to see if the RTC is keeping time.  
  if (! RTC.isrunning()) {
    Serial.println("RTC is NOT running!");
    // Sets the RTC to the time that this sketch was compiled 
    RTC.adjust(DateTime(F(__DATE__), F(__TIME__)));
  }
}
